# Fritzing sketch i2c_test (saved by Fritzing 0.9.2b)

parts:
  Part1 = Arduino Uno (Rev3)
  Raspberry_Pi2 = Raspberry Pi B rev2

nets:
  N1: Part1.A4/SDA, Raspberry_Pi2.GPIO_2
  N2: Part1.A5/SCL, Raspberry_Pi2.GPIO_3
  GND: Part1.GND, Raspberry_Pi2.GND
  VIN: Part1.VIN, Raspberry_Pi2.5V
